// Logisim project MIPSmulticycle.circ as structural Verilog: 10 circuits, main circuit main
module main (
  input  clk,
  input  rst
);

  wire button_1_out, button_2_out, button_3_out, button_4_out, button_5_out, clk_t, cU3B, cUHW, halt,
       isOpALU, jmpE, ldAB, ldIR, ldPC, lnk, mips_panel_1_clko, mips_panel_1_out_8, mips_panel_1_out_9,
       mips_panel_1_out_10, mips_panel_1_out_11, mips_panel_1_out_12, mips_panel_1_out_13,
       mips_panel_1_out_14, not_1_out, rDM, register_32b_2_p4, register_32b_4_p4, register_32b_5_p4, rMem,
       rst_t, wBREG, wDM, wMem;
  wire [0:0] or_1_out;
  wire [1:0] jmpM;
  wire [4:0] instruction_register_32b_1_rd, instruction_register_32b_1_rs, instruction_register_32b_1_rt,
       multiplexer_5_out, rt, shamt;
  wire [5:0] instruction_register_32b_1_funct, instruction_register_32b_1_opcode, multiplexer_4_out,
       multiplexer_8_out;
  wire [15:0] instruction_register_32b_1_immd, multiplexer_9_out;
  wire [25:0] instruction_register_32b_1_adrjmp;
  wire [31:0] adder_1_out, adder_2_out, adder_3_out, bit_extender_1_out, breg_1_value_1, breg_1_value_2,
       instruction_register_32b_1_q_for_visulization, memory_1_output, multiplexer_1_out, multiplexer_2_out,
       multiplexer_3_out, multiplexer_6_out, multiplexer_7_out, multiplexer_10_out, PC, register_32b_1_q,
       register_32b_1_q_for_visulization, register_32b_2_p6, register_32b_3_q,
       register_32b_3_q_for_visulization, register_32b_4_p1, register_32b_4_p6, register_32b_5_p6, vRs;
  wire [31:16] multiplexer_9_out_2;

  Adder #(.width(32)) adder_1 (
    .a(register_32b_1_q), .b(bit_extender_1_out), .out(adder_1_out), .cin(1'b0));  // open: cout
  Multiplexer #(.select(2), .width(32), .enable("false")) multiplexer_1 (
    .in0(breg_1_value_1), .in1({register_32b_1_q[31:26], instruction_register_32b_1_adrjmp}),
    .in2(adder_1_out), .in3(adder_1_out), .out(multiplexer_1_out), .sel(jmpM));
  MIPS_Panel mips_panel_1 (
    .btControl(button_1_out), .btRun(button_2_out), .btStep(button_3_out), .btReset(button_4_out),
    .btExtra(button_5_out), .clk(clk), .rst(rst), .out_8(mips_panel_1_out_8), .out_9(mips_panel_1_out_9),
    .out_10(mips_panel_1_out_10), .out_11(mips_panel_1_out_11), .out_12(mips_panel_1_out_12),
    .out_13(mips_panel_1_out_13), .out_14(mips_panel_1_out_14), .clkO(mips_panel_1_clko), .rstO(rst_t));
  LED led_1 (.in(mips_panel_1_out_13));
  LED led_2 (.in(mips_panel_1_out_14));
  Adder #(.width(32)) adder_2 (.a(register_32b_1_q), .b(32'h1), .out(adder_2_out));  // open: cin, cout
  LED led_3 (.in(mips_panel_1_out_8));
  Button button_1 (.out(button_1_out));
  register_32b register_32b_1 (
    .rst(rst_t), .clk(clk_t), .D(multiplexer_2_out), .Q(register_32b_1_q), .load(ldPC),
    .Q_for_visulization(register_32b_1_q_for_visulization));
  Multiplexer #(.width(32), .enable("false")) multiplexer_2 (
    .in0(adder_2_out), .in1(multiplexer_1_out), .out(multiplexer_2_out), .sel(jmpE));
  LED led_4 (.in(mips_panel_1_out_9));
  LED led_5 (.in(mips_panel_1_out_10));
  Button button_2 (.out(button_2_out));
  Button button_3 (.out(button_3_out));
  // Probe on register_32b_1_q_for_visulization
  LED led_6 (.in(mips_panel_1_out_11));
  Button button_4 (.out(button_4_out));
  Multiplexer #(.width(32), .enable("false")) multiplexer_3 (
    .in0(register_32b_1_q), .in1(memory_1_output), .out(multiplexer_3_out));  // open: sel
  LED led_7 (.in(mips_panel_1_out_12));
  Button button_5 (.out(button_5_out));
  Instruction_Register_32b instruction_register_32b_1 (
    .D(multiplexer_3_out), .load(ldIR), .clk(clk_t), .rst(rst_t),
    .Q_for_visulization(instruction_register_32b_1_q_for_visulization),
    .opCode(instruction_register_32b_1_opcode), .isOpALU(isOpALU), .Rs(instruction_register_32b_1_rs),
    .Rt(instruction_register_32b_1_rt), .Rd(instruction_register_32b_1_rd), .SHAMT(shamt),
    .funct(instruction_register_32b_1_funct), .adrJMP(instruction_register_32b_1_adrjmp),
    .immd(instruction_register_32b_1_immd));
  assign clk_t = ~halt ? mips_panel_1_clko : 1'bz;  // Controlled_Buffer controlled_buffer_1
  // Probe on instruction_register_32b_1_q_for_visulization
  Multiplexer #(.width(6), .enable("false")) multiplexer_4 (
    .in0({1'b0, rt}), .in1(instruction_register_32b_1_funct), .out(multiplexer_4_out), .sel(isOpALU));
  Control_Unit control_unit_1 (
    .opCode(instruction_register_32b_1_opcode), .wBREG(wBREG), .clk(clk_t), .rst(rst_t), .jmpE(jmpE),
    .jmpM(jmpM), .wDM(wDM), .rDM(rDM), .cUHW(cUHW), .cU3B(cU3B), .vRs(vRs), .\function (multiplexer_4_out),
    .link(lnk), .halt(halt));  // open: function_2, vRs_2, clk_2, rst_2, opCode_2
  assign bit_extender_1_out = {{16{instruction_register_32b_1_immd[15]}}, instruction_register_32b_1_immd};  // Bit_Extender bit_extender_1
  Multiplexer #(.select(2), .width(5), .enable("false")) multiplexer_5 (
    .in0(instruction_register_32b_1_rt), .in1(instruction_register_32b_1_rd),
    .in2(instruction_register_32b_1_rd), .in3({5{1'b1}}), .out(multiplexer_5_out), .sel({lnk, or_1_out[0]}));
  or or_1 (or_1_out[0], lnk, isOpALU);
  BREG breg_1 (
    .source_1(instruction_register_32b_1_rs), .target(multiplexer_5_out),
    .source_2(instruction_register_32b_1_rt), .\input (multiplexer_7_out), .clk(clk_t),
    .value_1(breg_1_value_1), .value_2(breg_1_value_2), .w(wBREG), .rst(rst_t));
  // register_32b register_32b_2: pin names not known; wires that end beside it: breg_1_value_1, ldAB, clk_t, register_32b_2_p4, rst_t, register_32b_2_p6
  register_32b register_32b_3 (
    .rst(rst_t), .clk(clk_t), .D(multiplexer_6_out), .Q(register_32b_3_q), .load(ldAB),
    .Q_for_visulization(register_32b_3_q_for_visulization));
  Multiplexer #(.width(32), .enable("false")) multiplexer_6 (
    .in0(bit_extender_1_out), .in1(breg_1_value_2), .out(multiplexer_6_out), .sel(isOpALU));
  Multiplexer #(.select(2), .width(32), .enable("false")) multiplexer_7 (
    .in0({multiplexer_9_out_2, multiplexer_9_out}), .in1({{16{1'b0}}, multiplexer_9_out}),
    .in2({{24{1'b0}}, multiplexer_9_out[7:0]}), .in3({{24{1'b0}}, multiplexer_9_out[7:0]}),
    .out(multiplexer_7_out), .sel({cU3B, cUHW}));
  // Probe on register_32b_2_p4
  // Probe on register_32b_3_q_for_visulization
  Multiplexer #(.width(6), .enable("false")) multiplexer_8 (
    .in0({6{1'b1}}), .in1(instruction_register_32b_1_funct), .out(multiplexer_8_out), .sel(isOpALU));
  // register_32b register_32b_4: pin names not known; wires that end beside it: register_32b_4_p1, ldIR, clk_t, register_32b_4_p4, rst_t, register_32b_4_p6
  ALU alu_1 (.A(register_32b_2_p6), .B(register_32b_3_q), .R(register_32b_4_p1), .\function (multiplexer_8_out));
  Adder #(.width(32)) adder_3 (.a(PC), .b(32'h1), .out(adder_3_out), .cin(1'b0));  // open: cout
  Multiplexer #(.width(32), .disabled(0), .enable("false")) multiplexer_9 (
    .in0(adder_3_out), .in1(multiplexer_10_out), .out({multiplexer_9_out_2, multiplexer_9_out}),
    .sel(not_1_out));
  // Probe on register_32b_4_p4
  Multiplexer #(.width(32), .disabled(0), .enable("false")) multiplexer_10 (
    .in0(register_32b_4_p6), .in1(register_32b_5_p6), .out(multiplexer_10_out), .sel(rDM));
  not not_1 (not_1_out, lnk);
  memory memory_1 (
    .Input(register_32b_4_p6), .wrt(clk_t), .clk(wMem), .ld(rMem), .rst(rst_t), .Output(memory_1_output));  // open: Adress
  // register_32b register_32b_5: pin names not known; wires that end beside it: memory_1_output, ldIR, clk_t, register_32b_5_p4, rst_t, register_32b_5_p6
  // Probe on register_32b_5_p4

  // Notes on the sheet:
  //   Jump
  //   Jump Register
  //        Branch's$(Relative Jumps)
  //   PC
  //   A
  //   B
  //   ALUout
  //   DMout
endmodule

module ALU (
  input  [31:0] A,
  input  [31:0] B,
  input  [5:0] \function ,
  output [31:0] R
);

  wire comparator_1_eq, isOpALU, multiplexer_5_out, multiplexer_6_out, multiplexer_8_out, registerInputs;
  wire [31:0] HI, LO, multiplexer_1_out, multiplexer_2_out, multiplexer_3_out, rA_q, rB_q, sum, undriven;

  // Probe on sum
  Adder #(.width(32)) adder_1 (.a(A), .b(B), .out(sum), .cin(1'b0));  // open: cout
  not not_1 (isOpALU, comparator_1_eq);
  Comparator #(.width(6)) comparator_1 (.a(\function ), .b({6{1'b1}}), .eq(comparator_1_eq));  // open: gt, lt
  Register #(.width(32), .Select("low")) rA (
    .D(A), .en(1'b1), .Q(rA_q), .clk(registerInputs), .clr(1'b0), .cs(1'b0), .preset(1'b0));
  Register #(.width(32), .Select("low")) rB (
    .D(B), .en(1'b1), .Q(rB_q), .clk(registerInputs), .clr(1'b0), .cs(1'b0), .preset(1'b0));
  // Probe on rA_q
  Multiplier #(.width(32)) multiplier_1 (.a(rA_q), .b(rB_q), .out(LO), .cin({32{1'b0}}), .cout(HI));
  // Probe on rB_q
  // Probe on LO
  // Probe on HI
  Multiplexer #(.select(5), .width(32), .enable("false")) multiplexer_1 (
    .in8(sum), .in16(HI), .in18(LO), .in24(undriven), .out(multiplexer_1_out), .sel(\function [4:0]));  // open: in0, in1, in2, in3, in4, in5, in6, in7, in9, in10, in11, in12, in13, in14, in15, in17, in19, in20, in21, in22, in23, in25, in26, in27, in28, in29, in30, in31
  Multiplexer #(.select(5), .width(32), .enable("false")) multiplexer_2 (
    .in0(sum), .out(multiplexer_2_out), .sel(\function [4:0]));  // open: in1, in2, in3, in4, in5, in6, in7, in8, in9, in10, in11, in12, in13, in14, in15, in16, in17, in18, in19, in20, in21, in22, in23, in24, in25, in26, in27, in28, in29, in30, in31
  // Probe on multiplexer_1_out
  Multiplexer #(.width(32), .enable("false")) multiplexer_3 (
    .in0(multiplexer_1_out), .in1(multiplexer_2_out), .out(multiplexer_3_out), .sel(\function [5]));
  Multiplexer #(.width(32), .enable("false")) multiplexer_4 (
    .in0(sum), .in1(multiplexer_3_out), .out(R), .sel(isOpALU));
  Multiplexer #(.select(5), .enable("false")) multiplexer_5 (
    .in0(1'b0), .in1(1'b0), .in2(1'b0), .in3(1'b0), .in4(1'b0), .in5(1'b0), .in6(1'b0), .in7(1'b0),
    .in8(1'b0), .in9(1'b0), .in10(1'b0), .in11(1'b0), .in12(1'b0), .in13(1'b0), .in14(1'b0), .in15(1'b0),
    .in16(1'b0), .in17(1'b0), .in18(1'b0), .in19(1'b0), .in20(1'b0), .in21(1'b0), .in22(1'b0), .in23(1'b0),
    .in24(1'b1), .in25(1'b0), .in26(1'b0), .in27(1'b0), .in28(1'b0), .in29(1'b0), .in30(1'b0), .in31(1'b0),
    .out(multiplexer_5_out), .sel(\function [4:0]));
  Multiplexer #(.select(5), .enable("false")) multiplexer_6 (
    .in0(1'b0), .in1(1'b0), .in2(1'b0), .in3(1'b0), .in4(1'b0), .in5(1'b0), .in6(1'b0), .in7(1'b0),
    .in8(1'b0), .in9(1'b0), .in10(1'b0), .in11(1'b0), .in12(1'b0), .in13(1'b0), .in14(1'b0), .in15(1'b0),
    .in16(1'b0), .in17(1'b0), .in18(1'b0), .in19(1'b0), .in20(1'b0), .in21(1'b0), .in22(1'b0), .in23(1'b0),
    .in24(1'b0), .in25(1'b0), .in26(1'b0), .in27(1'b0), .in28(1'b0), .in29(1'b0), .in30(1'b0), .in31(1'b0),
    .out(multiplexer_6_out), .sel(\function [4:0]));
  Multiplexer #(.enable("false")) multiplexer_7 (
    .in0(1'b0), .in1(multiplexer_8_out), .out(registerInputs), .sel(isOpALU));
  Multiplexer #(.enable("false")) multiplexer_8 (
    .in0(multiplexer_5_out), .in1(multiplexer_6_out), .out(multiplexer_8_out), .sel(\function [5]));

  // Other names for the same wires on the sheet: funct5LSb[4:0] = \function [4:0]; functMSb = \function [5]

  // Notes on the sheet:
  //   ADDI
  //   MFHI
  //   MFLO
  //   MULT
  //   XXX
  //   ADD
  //   ADDI
  //   MULT
  //   ADD
endmodule

module BREG (
  input  clk,
  input  rst,
  input  [31:0] \input ,
  input  [4:0] source_1,
  input  w,
  input  [4:0] target,
  input  [4:0] source_2,
  output [31:0] value_1,
  output [31:0] value_2
);

  wire decoder_1_out0, decoder_1_out1, decoder_1_out2, decoder_1_out3, decoder_1_out4, decoder_1_out5,
       decoder_1_out6, decoder_1_out7, decoder_1_out8, decoder_1_out9, decoder_1_out10, decoder_1_out11,
       decoder_1_out12, decoder_1_out13, decoder_1_out14, decoder_1_out15, decoder_1_out16, decoder_1_out17,
       decoder_1_out18, decoder_1_out19, decoder_1_out20, decoder_1_out21, decoder_1_out22, decoder_1_out23,
       decoder_1_out24, decoder_1_out25, decoder_1_out26, decoder_1_out27, decoder_1_out28, decoder_1_out29,
       decoder_1_out30, decoder_1_out31;
  wire [31:0] Q1, Q2, Q3, Q4, Q5, Q6, Q7, Q8, Q9, Q10, Q11, Q12, Q13, Q14, Q15, Q16, Q17, Q18, Q19, Q20, Q21,
       Q22, Q23, Q24, Q25, Q26, Q27, Q28, Q29, Q30, Q31;

  LED led_1 (.in(decoder_1_out0));
  Decoder #(.select(5), .disabled(0)) decoder_1 (
    .out0(decoder_1_out0), .out1(decoder_1_out1), .out2(decoder_1_out2), .out3(decoder_1_out3),
    .out4(decoder_1_out4), .out5(decoder_1_out5), .out6(decoder_1_out6), .out7(decoder_1_out7),
    .out8(decoder_1_out8), .out9(decoder_1_out9), .out10(decoder_1_out10), .out11(decoder_1_out11),
    .out12(decoder_1_out12), .out13(decoder_1_out13), .out14(decoder_1_out14), .out15(decoder_1_out15),
    .out16(decoder_1_out16), .out17(decoder_1_out17), .out18(decoder_1_out18), .out19(decoder_1_out19),
    .out20(decoder_1_out20), .out21(decoder_1_out21), .out22(decoder_1_out22), .out23(decoder_1_out23),
    .out24(decoder_1_out24), .out25(decoder_1_out25), .out26(decoder_1_out26), .out27(decoder_1_out27),
    .out28(decoder_1_out28), .out29(decoder_1_out29), .out30(decoder_1_out30), .out31(decoder_1_out31),
    .sel(target), .en(w));
  Register #(.width(32), .Select("high")) AT_R1 (
    .D(\input ), .en(decoder_1_out1), .Q(Q1), .clk(clk), .clr(rst), .cs(1'b1), .preset(1'b0));
  Register #(.width(32), .Select("high")) R2 (
    .D(\input ), .en(decoder_1_out2), .Q(Q2), .clk(clk), .clr(rst), .cs(1'b1), .preset(1'b0));
  Register #(.width(32), .Select("high")) R3 (
    .D(\input ), .en(decoder_1_out3), .Q(Q3), .clk(clk), .clr(rst), .cs(1'b1), .preset(1'b0));
  Register #(.width(32), .Select("high")) R28 (
    .D(\input ), .en(decoder_1_out28), .Q(Q28), .clk(clk), .clr(rst), .cs(1'b1), .preset(1'b0));
  Register #(.width(32), .Select("high")) R29 (
    .D(\input ), .en(decoder_1_out29), .Q(Q29), .clk(clk), .clr(rst), .cs(1'b1), .preset(1'b0));
  Register #(.width(32), .Select("high")) R30 (
    .D(\input ), .en(decoder_1_out30), .Q(Q30), .clk(clk), .clr(rst), .cs(1'b1), .preset(1'b0));
  Register #(.width(32), .Select("high")) Return_Adress__R31 (
    .D(\input ), .en(decoder_1_out31), .Q(Q31), .clk(clk), .clr(rst), .cs(1'b1), .preset(1'b0));
  Register #(.width(32), .Select("high")) R4 (
    .D(\input ), .en(decoder_1_out4), .Q(Q4), .clk(clk), .clr(rst), .cs(1'b1), .preset(1'b0));
  Register #(.width(32), .Select("high")) R5 (
    .D(\input ), .en(decoder_1_out5), .Q(Q5), .clk(clk), .clr(rst), .cs(1'b1), .preset(1'b0));
  Register #(.width(32), .Select("high")) R6 (
    .D(\input ), .en(decoder_1_out6), .Q(Q6), .clk(clk), .clr(rst), .cs(1'b1), .preset(1'b0));
  Register #(.width(32), .Select("high")) R7 (
    .D(\input ), .en(decoder_1_out7), .Q(Q7), .clk(clk), .clr(rst), .cs(1'b1), .preset(1'b0));
  Register #(.width(32), .Select("high")) R24 (
    .D(\input ), .en(decoder_1_out24), .Q(Q24), .clk(clk), .clr(rst), .cs(1'b1), .preset(1'b0));
  Register #(.width(32), .Select("high")) R25 (
    .D(\input ), .en(decoder_1_out25), .Q(Q25), .clk(clk), .clr(rst), .cs(1'b1), .preset(1'b0));
  Register #(.width(32), .Select("high")) R26 (
    .D(\input ), .en(decoder_1_out26), .Q(Q26), .clk(clk), .clr(rst), .cs(1'b1), .preset(1'b0));
  Register #(.width(32), .Select("high")) R27 (
    .D(\input ), .en(decoder_1_out27), .Q(Q27), .clk(clk), .clr(rst), .cs(1'b1), .preset(1'b0));
  Register #(.width(32), .Select("high")) R8 (
    .D(\input ), .en(decoder_1_out8), .Q(Q8), .clk(clk), .clr(rst), .cs(1'b1), .preset(1'b0));
  Register #(.width(32), .Select("high")) R9 (
    .D(\input ), .en(decoder_1_out9), .Q(Q9), .clk(clk), .clr(rst), .cs(1'b1), .preset(1'b0));
  Register #(.width(32), .Select("high")) R10 (
    .D(\input ), .en(decoder_1_out10), .Q(Q10), .clk(clk), .clr(rst), .cs(1'b1), .preset(1'b0));
  Register #(.width(32), .Select("high")) R11 (
    .D(\input ), .en(decoder_1_out11), .Q(Q11), .clk(clk), .clr(rst), .cs(1'b1), .preset(1'b0));
  Register #(.width(32), .Select("high")) R20 (
    .D(\input ), .en(decoder_1_out20), .Q(Q20), .clk(clk), .clr(rst), .cs(1'b1), .preset(1'b0));
  Register #(.width(32), .Select("high")) R21 (
    .D(\input ), .en(decoder_1_out21), .Q(Q21), .clk(clk), .clr(rst), .cs(1'b1), .preset(1'b0));
  Register #(.width(32), .Select("high")) R22 (
    .D(\input ), .en(decoder_1_out22), .Q(Q22), .clk(clk), .clr(rst), .cs(1'b1), .preset(1'b0));
  Register #(.width(32), .Select("high")) R23 (
    .D(\input ), .en(decoder_1_out23), .Q(Q23), .clk(clk), .clr(rst), .cs(1'b1), .preset(1'b0));
  Register #(.width(32), .Select("high")) R12 (
    .D(\input ), .en(decoder_1_out12), .Q(Q12), .clk(clk), .clr(rst), .cs(1'b1), .preset(1'b0));
  Register #(.width(32), .Select("high")) R13 (
    .D(\input ), .en(decoder_1_out13), .Q(Q13), .clk(clk), .clr(rst), .cs(1'b1), .preset(1'b0));
  Register #(.width(32), .Select("high")) R14 (
    .D(\input ), .en(decoder_1_out14), .Q(Q14), .clk(clk), .clr(rst), .cs(1'b1), .preset(1'b0));
  Register #(.width(32), .Select("high")) R15 (
    .D(\input ), .en(decoder_1_out15), .Q(Q15), .clk(clk), .clr(rst), .cs(1'b1), .preset(1'b0));
  Register #(.width(32), .Select("high")) R16 (
    .D(\input ), .en(decoder_1_out16), .Q(Q16), .clk(clk), .clr(rst), .cs(1'b1), .preset(1'b0));
  Register #(.width(32), .Select("high")) R17 (
    .D(\input ), .en(decoder_1_out17), .Q(Q17), .clk(clk), .clr(rst), .cs(1'b1), .preset(1'b0));
  Register #(.width(32), .Select("high")) R18 (
    .D(\input ), .en(decoder_1_out18), .Q(Q18), .clk(clk), .clr(rst), .cs(1'b1), .preset(1'b0));
  Register #(.width(32), .Select("high")) R19 (
    .D(\input ), .en(decoder_1_out19), .Q(Q19), .clk(clk), .clr(rst), .cs(1'b1), .preset(1'b0));
  Multiplexer #(.select(5), .width(32), .enable("false")) multiplexer_1 (
    .in0({32{1'b0}}), .in1(Q1), .in2(Q2), .in3(Q3), .in4(Q4), .in5(Q5), .in6(Q6), .in7(Q7), .in8(Q8),
    .in9(Q9), .in10(Q10), .in11(Q11), .in12(Q12), .in13(Q13), .in14(Q14), .in15(Q15), .in16(Q16), .in17(Q17),
    .in18(Q18), .in19(Q19), .in20(Q20), .in21(Q21), .in22(Q22), .in23(Q23), .in24(Q24), .in25(Q25),
    .in26(Q26), .in27(Q27), .in28(Q28), .in29(Q29), .in30(Q30), .in31(Q31), .out(value_1), .sel(source_1));
  Multiplexer #(.select(5), .width(32), .enable("false")) multiplexer_2 (
    .in0({32{1'b0}}), .in1(Q1), .in2(Q2), .in3(Q3), .in4(Q4), .in5(Q5), .in6(Q6), .in7(Q7), .in8(Q8),
    .in9(Q9), .in10(Q10), .in11(Q11), .in12(Q12), .in13(Q13), .in14(Q14), .in15(Q15), .in16(Q16), .in17(Q17),
    .in18(Q18), .in19(Q19), .in20(Q20), .in21(Q21), .in22(Q22), .in23(Q23), .in24(Q24), .in25(Q25),
    .in26(Q26), .in27(Q27), .in28(Q28), .in29(Q29), .in30(Q30), .in31(Q31), .out(value_2), .sel(source_2));

  // Other names for the same wires on the sheet: D[31:0] = \input 

  // Notes on the sheet:
  //   ZERO(R0)
endmodule

module Control_Unit (
  input  [5:0] \function ,
  input  [31:0] vRs,
  input  clk,
  input  rst,
  input  [5:0] opCode,
  input  [5:0] function_2,
  input  [31:0] vRs_2,
  input  clk_2,
  input  rst_2,
  input  [5:0] opCode_2,
  output wBREG,
  output wDM,
  output rDM,
  output cUHW,
  output cU3B,
  output jmpE,
  output link,
  output [1:0] jmpM,
  output halt
);

  wire Branch_Analyzer_jmpe, comparator_1_eq, comparator_2_eq, Link_Analyzer_link, multiplexer_1_out,
       multiplexer_2_out, multiplexer_4_out, multiplexer_5_out, multiplexer_7_out, multiplexer_8_out,
       multiplexer_10_out, multiplexer_12_out, multiplexer_13_out, multiplexer_14_out, multiplexer_16_out,
       multiplexer_17_out, multiplexer_19_out, multiplexer_20_out, not_1_out;
  wire [31:0] act_state_q, outputs_data;

  Comparator #(.width(6)) comparator_1 (.a(\function ), .b(6'b001000), .eq(comparator_1_eq));  // open: gt, lt
  Comparator #(.width(6)) comparator_2 (.a(\function ), .b(6'b001000), .eq(comparator_2_eq));  // open: gt, lt
  not not_1 (not_1_out, comparator_1_eq);
  // Probe on opCode[4:0]
  and and_1 (jmpM[1], ~opCode[1], jmpM[0]);  // AND_Gate
  or or_1 (jmpM[0], opCode[2], opCode[1], opCode[0]);
  Multiplexer #(.select(5), .enable("false")) multiplexer_1 (
    .in0(not_1_out), .in1(1'b1), .in2(1'b0), .in3(1'b0), .in4(1'b0), .in5(1'b0), .in6(1'b0), .in7(1'b0),
    .in8(1'b1), .in9(1'b0), .in10(1'b0), .in11(1'b0), .in12(1'b0), .in13(1'b0), .in14(1'b0), .in15(1'b0),
    .in16(1'b0), .in17(1'b0), .in18(1'b0), .in19(1'b0), .in20(1'b0), .in21(1'b0), .in22(1'b0), .in23(1'b0),
    .in24(1'b0), .in25(1'b0), .in26(1'b0), .in27(1'b0), .in28(1'b0), .in29(1'b0), .in30(1'b0), .in31(1'b0),
    .out(multiplexer_1_out), .sel(opCode[4:0]));
  Multiplexer #(.select(5), .enable("false")) multiplexer_2 (
    .in0(1'b0), .in1(1'b0), .in2(1'b0), .in3(1'b0), .in4(1'b1), .in5(1'b0), .in6(1'b0), .in7(1'b0),
    .in8(1'b0), .in9(1'b0), .in10(1'b0), .in11(1'b0), .in12(1'b0), .in13(1'b0), .in14(1'b0), .in15(1'b0),
    .in16(1'b0), .in17(1'b0), .in18(1'b0), .in19(1'b0), .in20(1'b0), .in21(1'b0), .in22(1'b0), .in23(1'b0),
    .in24(1'b0), .in25(1'b0), .in26(1'b0), .in27(1'b0), .in28(1'b0), .in29(1'b0), .in30(1'b0), .in31(1'b0),
    .out(multiplexer_2_out), .sel(opCode[4:0]));
  Comparator #(.width(6)) comparator_3 (.a(opCode), .b({6{1'b1}}), .eq(halt));  // open: gt, lt
  Multiplexer #(.enable("false")) multiplexer_3 (
    .in0(multiplexer_1_out), .in1(multiplexer_2_out), .out(wBREG), .sel(opCode[5]));
  Multiplexer #(.select(5), .enable("false")) multiplexer_4 (
    .in0(1'b0), .in1(1'b0), .in2(1'b0), .in3(1'b0), .in4(1'b0), .in5(1'b0), .in6(1'b0), .in7(1'b0),
    .in8(1'b0), .in9(1'b0), .in10(1'b0), .in11(1'b0), .in12(1'b0), .in13(1'b0), .in14(1'b0), .in15(1'b0),
    .in16(1'b0), .in17(1'b0), .in18(1'b0), .in19(1'b0), .in20(1'b0), .in21(1'b0), .in22(1'b0), .in23(1'b0),
    .in24(1'b0), .in25(1'b0), .in26(1'b0), .in27(1'b0), .in28(1'b0), .in29(1'b0), .in30(1'b0), .in31(1'b0),
    .out(multiplexer_4_out), .sel(opCode[4:0]));
  Multiplexer #(.select(5), .enable("false")) multiplexer_5 (
    .in0(1'b0), .in1(1'b0), .in2(1'b0), .in3(1'b0), .in4(1'b0), .in5(1'b0), .in6(1'b0), .in7(1'b0),
    .in8(1'b0), .in9(1'b0), .in10(1'b0), .in11(1'b0), .in12(1'b0), .in13(1'b0), .in14(1'b0), .in15(1'b0),
    .in16(1'b0), .in17(1'b0), .in18(1'b0), .in19(1'b0), .in20(1'b0), .in21(1'b0), .in22(1'b0), .in23(1'b0),
    .in24(1'b0), .in25(1'b0), .in26(1'b0), .in27(1'b0), .in28(1'b0), .in29(1'b0), .in30(1'b0), .in31(1'b0),
    .out(multiplexer_5_out), .sel(opCode[4:0]));
  Register #(.width(32), .Select("high")) act_state (.Q(act_state_q));  // open: D, en, clk, clr
  Multiplexer #(.enable("false")) multiplexer_6 (
    .in0(multiplexer_4_out), .in1(multiplexer_5_out), .out(wDM), .sel(opCode[5]));
  ROM #(.Select("low")) rom_1 ();  // open: addr, data
  Multiplexer #(.select(5), .enable("false")) multiplexer_7 (
    .in0(1'b0), .in1(1'b0), .in2(1'b0), .in3(1'b0), .in4(1'b0), .in5(1'b0), .in6(1'b0), .in7(1'b0),
    .in8(1'b0), .in9(1'b0), .in10(1'b0), .in11(1'b0), .in12(1'b0), .in13(1'b0), .in14(1'b0), .in15(1'b0),
    .in16(1'b0), .in17(1'b0), .in18(1'b0), .in19(1'b0), .in20(1'b0), .in21(1'b0), .in22(1'b0), .in23(1'b0),
    .in24(1'b0), .in25(1'b0), .in26(1'b0), .in27(1'b0), .in28(1'b0), .in29(1'b0), .in30(1'b0), .in31(1'b0),
    .out(multiplexer_7_out), .sel(opCode[4:0]));
  Multiplexer #(.select(5), .enable("false")) multiplexer_8 (
    .in0(1'b0), .in1(1'b0), .in2(1'b0), .in3(1'b0), .in4(1'b1), .in5(1'b0), .in6(1'b0), .in7(1'b0),
    .in8(1'b0), .in9(1'b0), .in10(1'b0), .in11(1'b0), .in12(1'b0), .in13(1'b0), .in14(1'b0), .in15(1'b0),
    .in16(1'b0), .in17(1'b0), .in18(1'b0), .in19(1'b0), .in20(1'b0), .in21(1'b0), .in22(1'b0), .in23(1'b0),
    .in24(1'b0), .in25(1'b0), .in26(1'b0), .in27(1'b0), .in28(1'b0), .in29(1'b0), .in30(1'b0), .in31(1'b0),
    .out(multiplexer_8_out), .sel(opCode[4:0]));
  ROM #(.addrWidth(24), .dataWidth(32), .Select("high")) outputs (
    .addr(act_state_q[23:0]), .data(outputs_data), .sel(1'b1));
  Multiplexer #(.enable("false")) multiplexer_9 (
    .in0(multiplexer_7_out), .in1(multiplexer_8_out), .out(rDM), .sel(opCode[5]));
  Multiplexer #(.select(5), .enable("false")) multiplexer_10 (
    .in0(1'b0), .in1(1'b0), .in2(1'b0), .in3(1'b0), .in4(1'b0), .in5(1'b0), .in6(1'b0), .in7(1'b0),
    .in8(1'b0), .in9(1'b0), .in10(1'b0), .in11(1'b0), .in12(1'b0), .in13(1'b0), .in14(1'b0), .in15(1'b0),
    .in16(1'b0), .in17(1'b0), .in18(1'b0), .in19(1'b0), .in20(1'b0), .in21(1'b0), .in22(1'b0), .in23(1'b0),
    .in24(1'b0), .in25(1'b0), .in26(1'b0), .in27(1'b0), .in28(1'b0), .in29(1'b0), .in30(1'b0), .in31(1'b0),
    .out(multiplexer_10_out), .sel(opCode[4:0]));
  Multiplexer #(.enable("false")) multiplexer_11 (
    .in0(multiplexer_10_out), .in1(multiplexer_12_out), .out(cUHW), .sel(opCode[5]));
  Multiplexer #(.select(5), .enable("false")) multiplexer_12 (
    .in0(1'b0), .in1(1'b0), .in2(1'b0), .in3(1'b0), .in4(1'b1), .in5(1'b0), .in6(1'b0), .in7(1'b0),
    .in8(1'b0), .in9(1'b0), .in10(1'b0), .in11(1'b0), .in12(1'b0), .in13(1'b0), .in14(1'b0), .in15(1'b0),
    .in16(1'b0), .in17(1'b0), .in18(1'b0), .in19(1'b0), .in20(1'b0), .in21(1'b0), .in22(1'b0), .in23(1'b0),
    .in24(1'b0), .in25(1'b0), .in26(1'b0), .in27(1'b0), .in28(1'b0), .in29(1'b0), .in30(1'b0), .in31(1'b0),
    .out(multiplexer_12_out), .sel(opCode[4:0]));
  Multiplexer #(.select(5), .enable("false")) multiplexer_13 (
    .in0(1'b0), .in1(1'b0), .in2(1'b0), .in3(1'b0), .in4(1'b0), .in5(1'b0), .in6(1'b0), .in7(1'b0),
    .in8(1'b0), .in9(1'b0), .in10(1'b0), .in11(1'b0), .in12(1'b0), .in13(1'b0), .in14(1'b0), .in15(1'b0),
    .in16(1'b0), .in17(1'b0), .in18(1'b0), .in19(1'b0), .in20(1'b0), .in21(1'b0), .in22(1'b0), .in23(1'b0),
    .in24(1'b0), .in25(1'b0), .in26(1'b0), .in27(1'b0), .in28(1'b0), .in29(1'b0), .in30(1'b0), .in31(1'b0),
    .out(multiplexer_13_out), .sel(opCode[4:0]));
  Multiplexer #(.select(5), .enable("false")) multiplexer_14 (
    .in0(1'b0), .in1(1'b0), .in2(1'b0), .in3(1'b0), .in4(1'b1), .in5(1'b0), .in6(1'b0), .in7(1'b0),
    .in8(1'b0), .in9(1'b0), .in10(1'b0), .in11(1'b0), .in12(1'b0), .in13(1'b0), .in14(1'b0), .in15(1'b0),
    .in16(1'b0), .in17(1'b0), .in18(1'b0), .in19(1'b0), .in20(1'b0), .in21(1'b0), .in22(1'b0), .in23(1'b0),
    .in24(1'b0), .in25(1'b0), .in26(1'b0), .in27(1'b0), .in28(1'b0), .in29(1'b0), .in30(1'b0), .in31(1'b0),
    .out(multiplexer_14_out), .sel(opCode[4:0]));
  Multiplexer #(.enable("false")) multiplexer_15 (
    .in0(multiplexer_13_out), .in1(multiplexer_14_out), .out(cU3B), .sel(opCode[5]));
  branch_analyzer Branch_Analyzer (.vRs(vRs), .jmpE(Branch_Analyzer_jmpe), .\function (\function ));
  Multiplexer #(.select(5), .enable("false")) multiplexer_16 (
    .in0(comparator_1_eq), .in1(Branch_Analyzer_jmpe), .in2(1'b0), .in3(1'b0), .in4(1'b0), .in5(1'b0),
    .in6(1'b0), .in7(1'b0), .in8(1'b0), .in9(1'b0), .in10(1'b0), .in11(1'b0), .in12(1'b0), .in13(1'b0),
    .in14(1'b0), .in15(1'b0), .in16(1'b0), .in17(1'b0), .in18(1'b0), .in19(1'b0), .in20(1'b0), .in21(1'b0),
    .in22(1'b0), .in23(1'b0), .in24(1'b0), .in25(1'b0), .in26(1'b0), .in27(1'b0), .in28(1'b0), .in29(1'b0),
    .in30(1'b0), .in31(1'b0), .out(multiplexer_16_out), .sel(opCode[4:0]));
  Multiplexer #(.select(5), .enable("false")) multiplexer_17 (
    .in0(1'b0), .in1(1'b0), .in2(1'b0), .in3(1'b0), .in4(1'b0), .in5(1'b0), .in6(1'b0), .in7(1'b0),
    .in8(1'b0), .in9(1'b0), .in10(1'b0), .in11(1'b0), .in12(1'b0), .in13(1'b0), .in14(1'b0), .in15(1'b0),
    .in16(1'b0), .in17(1'b0), .in18(1'b0), .in19(1'b0), .in20(1'b0), .in21(1'b0), .in22(1'b0), .in23(1'b0),
    .in24(1'b0), .in25(1'b0), .in26(1'b0), .in27(1'b0), .in28(1'b0), .in29(1'b0), .in30(1'b0), .in31(1'b0),
    .out(multiplexer_17_out), .sel(opCode[4:0]));
  Multiplexer #(.enable("false")) multiplexer_18 (
    .in0(multiplexer_16_out), .in1(multiplexer_17_out), .out(jmpE), .sel(opCode[5]));
  link_analyzer Link_Analyzer (.jmpE(jmpE), .\function (\function ), .link(Link_Analyzer_link));
  Multiplexer #(.select(5), .enable("false")) multiplexer_19 (
    .in0(1'b0), .in1(Link_Analyzer_link), .in2(1'b0), .in3(1'b0), .in4(1'b0), .in5(1'b0), .in6(1'b0),
    .in7(1'b0), .in8(1'b0), .in9(1'b0), .in10(1'b0), .in11(1'b0), .in12(1'b0), .in13(1'b0), .in14(1'b0),
    .in15(1'b0), .in16(1'b0), .in17(1'b0), .in18(1'b0), .in19(1'b0), .in20(1'b0), .in21(1'b0), .in22(1'b0),
    .in23(1'b0), .in24(1'b0), .in25(1'b0), .in26(1'b0), .in27(1'b0), .in28(1'b0), .in29(1'b0), .in30(1'b0),
    .in31(1'b0), .out(multiplexer_19_out), .sel(opCode[4:0]));
  Multiplexer #(.select(5), .enable("false")) multiplexer_20 (
    .in0(1'b0), .in1(1'b0), .in2(1'b0), .in3(1'b0), .in4(1'b0), .in5(1'b0), .in6(1'b0), .in7(1'b0),
    .in8(1'b0), .in9(1'b0), .in10(1'b0), .in11(1'b0), .in12(1'b0), .in13(1'b0), .in14(1'b0), .in15(1'b0),
    .in16(1'b0), .in17(1'b0), .in18(1'b0), .in19(1'b0), .in20(1'b0), .in21(1'b0), .in22(1'b0), .in23(1'b0),
    .in24(1'b0), .in25(1'b0), .in26(1'b0), .in27(1'b0), .in28(1'b0), .in29(1'b0), .in30(1'b0), .in31(1'b0),
    .out(multiplexer_20_out), .sel(opCode[4:0]));
  Multiplexer #(.enable("false")) multiplexer_21 (
    .in0(multiplexer_19_out), .in1(multiplexer_20_out), .out(link), .sel(opCode[5]));

  assign function_2 = \function ;
  assign vRs_2 = vRs;

  // Notes on the sheet:
  //   wBREG:
  //         Write sign to BREG
  //   jmpM:
  //         Jump Mode sign
  //   CBranch's
  //   ADDI
  //   LBU
  //         Write sign to Data Memory
  //   wDM:
  //   ADDI
  //   LBU
  //   rDM:
  //         Read from Data $Memory to BREG sign
  //   ADDI
  //   LBU
  //   cUHW:
  //   Clear Upper Half-Word $sign on data to BREG load
  //   ADDI
  //   LBU
  //   cU3B:
  //   Clear Upper 3 Bytes on$data to BREG load
  //   ADDI
  //   LBU
  //         Jump Enable sign
  //   jmpE:
  //   link:
  //   Link sign. Save PC+4 in R31
endmodule

module branch_analyzer (
  input  [31:0] vRs,
  input  [5:0] \function ,
  output jmpE
);

  wire comparator_1_lt;

  Comparator #(.width(32)) comparator_1 (.a(vRs), .b({32{1'b0}}), .lt(comparator_1_lt));  // open: gt, eq
  Multiplexer #(.select(5), .disabled(0), .enable("false")) multiplexer_1 (
    .in0(1'b0), .in1(1'b0), .in2(1'b0), .in3(1'b0), .in4(1'b0), .in5(1'b0), .in6(1'b0), .in7(1'b0),
    .in8(1'b0), .in9(1'b0), .in10(1'b0), .in11(1'b0), .in12(1'b0), .in13(1'b0), .in14(1'b0), .in15(1'b0),
    .in16(comparator_1_lt), .in17(1'b0), .in18(1'b0), .in19(1'b0), .in20(1'b0), .in21(1'b0), .in22(1'b0),
    .in23(1'b0), .in24(1'b0), .in25(1'b0), .in26(1'b0), .in27(1'b0), .in28(1'b0), .in29(1'b0), .in30(1'b0),
    .in31(1'b0), .out(jmpE), .sel(\function [4:0]));
  // Probe on \function [4:0]

  // Notes on the sheet:
  //   BLTZAL
endmodule

module link_analyzer (
  input  jmpE,
  input  [5:0] \function ,
  output link
);

  Multiplexer #(.select(5), .disabled(0), .enable("false")) multiplexer_1 (
    .in0(1'b0), .in1(1'b0), .in2(1'b0), .in3(1'b0), .in4(1'b0), .in5(1'b0), .in6(1'b0), .in7(1'b0),
    .in8(1'b0), .in9(1'b0), .in10(1'b0), .in11(1'b0), .in12(1'b0), .in13(1'b0), .in14(1'b0), .in15(1'b0),
    .in16(jmpE), .in17(1'b0), .in18(1'b0), .in19(1'b0), .in20(1'b0), .in21(1'b0), .in22(1'b0), .in23(1'b0),
    .in24(1'b0), .in25(1'b0), .in26(1'b0), .in27(1'b0), .in28(1'b0), .in29(1'b0), .in30(1'b0), .in31(1'b0),
    .out(link), .sel(\function [4:0]));

  // Notes on the sheet:
  //   BLTZAL
endmodule

module MIPS_Panel (
  input  btControl,
  input  btRun,
  input  btStep,
  input  btReset,
  input  btExtra,
  input  clk,
  input  rst,
  output out_8,
  output out_9,
  output out_10,
  output out_11,
  output out_12,
  output out_13,
  output out_14,
  output clkO,
  output rstO
);

  wire clock_1_out, controlled_buffer_1_out, d_ff_1_qn, d_ff_2_q, d_ff_2_qn, multiplexer_1_out, not_1_out;

  D_Flip_Flop d_ff_1 (.clk(btControl), .D(d_ff_1_qn), .Q(out_8), .Qn(d_ff_1_qn), .preset(1'b0), .reset(1'b0));
  D_Flip_Flop d_ff_2 (.clk(btRun), .D(d_ff_2_qn), .Q(d_ff_2_q), .Qn(d_ff_2_qn), .preset(1'b0), .reset(btStep));
  assign controlled_buffer_1_out = d_ff_2_q ? clock_1_out : 1'bz;  // Controlled_Buffer controlled_buffer_1
  Clock clock_1 (.out(clock_1_out));
  assign out_9 = out_8 ? d_ff_2_q : 1'bz;  // Controlled_Buffer controlled_buffer_2
  assign out_10 = out_8 ? btStep : 1'bz;  // Controlled_Buffer controlled_buffer_3
  assign out_11 = out_8 ? btReset : 1'bz;  // Controlled_Buffer controlled_buffer_4
  assign out_12 = out_8 ? btExtra : 1'bz;  // Controlled_Buffer controlled_buffer_5
  assign out_13 = ~out_8 ? clk : 1'bz;  // Controlled_Buffer controlled_buffer_6
  assign out_14 = ~out_8 ? rst : 1'bz;  // Controlled_Buffer controlled_buffer_7
  Multiplexer #(.enable("false")) multiplexer_1 (
    .in0(btStep), .in1(controlled_buffer_1_out), .out(multiplexer_1_out), .sel(d_ff_2_q));
  not not_1 (not_1_out, out_8);
  Multiplexer #(.enable("false")) multiplexer_2 (.in0(multiplexer_1_out), .in1(clk), .out(clkO), .sel(not_1_out));
  Multiplexer #(.enable("false")) multiplexer_3 (.in0(btReset), .in1(rst), .out(rstO), .sel(not_1_out));
endmodule

module register_32b (
  input  [31:0] D,
  input  load,
  input  clk,
  input  rst,
  output [31:0] Q,
  output [31:0] Q_for_visulization
);

  Register #(.width(32), .Select("high")) register_1 (
    .D(D), .en(load), .Q(Q), .clk(clk), .clr(rst), .cs(1'b1), .preset(1'b0));

  assign Q_for_visulization = Q;
endmodule

module Instruction_Register_32b (
  input  [31:0] D,
  input  load,
  input  clk,
  input  rst,
  output [5:0] opCode,
  output isOpALU,
  output [4:0] Rs,
  output [4:0] Rt,
  output [4:0] Rd,
  output [4:0] SHAMT,
  output [31:0] Q_for_visulization,
  output [5:0] funct,
  output [15:0] immd,
  output [25:0] adrJMP
);

  Register #(.width(32), .Select("high")) register_1 (
    .D(D), .en(load), .Q({opCode, adrJMP}), .clk(clk), .clr(rst), .cs(1'b1), .preset(1'b0));
  Comparator #(.width(6)) comparator_1 (.a(opCode), .b({6{1'b0}}), .eq(isOpALU));  // open: gt, lt

  assign funct = adrJMP[5:0];
  assign immd = adrJMP[15:0];
  assign Q_for_visulization = {opCode, adrJMP};
  assign Rd = adrJMP[15:11];
  assign Rs = adrJMP[25:21];
  assign Rt = adrJMP[20:16];
  assign SHAMT = adrJMP[10:6];
endmodule

module memory (
  input  [31:0] Adress,
  input  [31:0] Input,
  input  wrt,
  input  clk,
  input  ld,
  input  rst,
  output [31:0] Output
);

  wire comparator_1_gt;
  wire [31:0] ram_1_data, ram_2_data;

  Comparator #(.width(32)) comparator_1 (.a(Adress), .b(32'hffff), .gt(comparator_1_gt));  // open: eq, lt
  RAM #(.addrWidth(16), .dataWidth(32), .bus("separate"), .Select("high"), .simpleMode("false")) ram_1 (
    .addr(Adress[15:0]), .din(Input), .data(ram_1_data), .str(wrt), .sel(1'b1), .clk(clk), .ld(ld), .clr(rst));
  RAM #(.addrWidth(16), .dataWidth(32), .bus("separate"), .Select("high"), .simpleMode("false")) ram_2 (
    .addr(Adress[31:16]), .din(Input), .data(ram_2_data), .str(wrt), .sel(1'b1), .clk(clk), .ld(ld), .clr(rst));
  Multiplexer #(.width(32), .enable("false")) multiplexer_1 (
    .in0(ram_1_data), .in1(ram_2_data), .out(Output), .sel(comparator_1_gt));
endmodule
